# Fritzing sketch Connection (saved by Fritzing 0.9.3b)
breadboards: 1

parts:
  ESP32 = Adafruit HUZZAH32 ESP32 Feather [part_number="Adafruit #3405"]
  DS3231 = ZS-042 RTC Module
  SD = MicroSD Card Module
  U1 = RJ45 Jack [package=rj45-8]
  RS422toTLL = IC, DIP package, 16 pins [chip_label=RS422]
  S1 = Pushbutton [package="[THT]"]
  LED1 = LED - 5mm [color="Red (633nm)" package="5 mm [THT]"]
  R1 = Resistor [tolerance=±5% resistance=220 package=THT]

nets:
  N1: ESP32.IO21, DS3231.SDA
  N2: ESP32.MISO, SD.MISO
  N3: ESP32.MOSI, SD.SCK
  N4: ESP32.A1_DAC1, RS422toTLL.pin2
  N5: ESP32.A0_DAC2, RS422toTLL.pin3
  GND: ESP32.GND, DS3231.GND, SD.GND, U1.8, RS422toTLL.pin4, RS422toTLL.pin12, S1.Pin_3, S1.Pin_4, R1.Pin_0
  3.3V: ESP32.3.3V, SD.VCC
  N6: ESP32.VBUS, DS3231.VCC, RS422toTLL.pin1
  N7: ESP32.IO33_A9, S1.Pin_2
  N8: ESP32.IO32_A7, LED1.anode
  N9: ESP32.IO14_A6, SD.CS
  N10: ESP32.SCL, DS3231.SCL
  N11: ESP32.SDA, SD.MOSI
  N12: U1.3, RS422toTLL.pin15
  N13: U1.4, RS422toTLL.pin16
  N14: U1.5, RS422toTLL.pin13
  N15: U1.6, RS422toTLL.pin14
  N16: LED1.cathode, R1.Pin_1

notes:
  Data+
  Data-
  Clock+
  Clock-
  GND
  Encoder
  <-
